# Fritzing sketch temp_ds18b20 (saved by Fritzing 0.9.2b)
circuit board: 18.0246cm x 9.25688cm
breadboards: 1

parts:
  Raspberry_Pi1 = Raspberry Pi B+
  U1 = LCD-16X2 [package=lcd-16x2_noholes]
  R1 = Rotary Potentiometer (Small) [maximum_resistance=10kΩ package=THT]
  R2 = Rotary Potentiometer (Small) [maximum_resistance=10kΩ package=THT]
  DS1 = DS18B20 1-Wire Temperature Sensor [part_number=DS18B20]
  R3 = Resistor [tolerance=±5% resistance=4.7k package="0603 [SMD]"]

nets:
  N1: Raspberry_Pi1.GPIO4, DS1.DQ, R3.Pin_0, R3.Pin_1
  GND: Raspberry_Pi1.GND, U1.VSS, U1.R_W, U1.K, DS1.GND
  N2: Raspberry_Pi1.GPIO11, U1.DB7
  N3: Raspberry_Pi1.GPIO5, U1.DB6
  N4: Raspberry_Pi1.GPIO6, U1.DB5
  N5: Raspberry_Pi1.GPIO13, U1.DB4
  N6: Raspberry_Pi1.GPIO19, U1.E
  N7: Raspberry_Pi1.GPIO26, U1.RS
  VDD: Raspberry_Pi1.5V, U1.VDD, R1.leg1, R2.leg1, DS1.VDD
  N8: U1.VO, R2.wiper
  N9: U1.A, R1.wiper
